# Fritzing sketch TickTackBoom (saved by Fritzing 0.9.3b)
circuit board: 8.5298cm x 3.1298cm
breadboards: 1

parts:
  Arduino_Pro_Micro = Arduino Pro micro
  OLED = female pin header, 4 pins [form="♀ (female)"]
  Buzzer = Buzzer 12mm [package=buzzer-12mm]
  S1 = Momentary Switch [package=tactile-pth]
  S2 = Momentary Switch [package=tactile-pth]

nets:
  N1: Arduino_Pro_Micro.GRD, OLED.pin3, Buzzer.2, S1.1, S2.4
  N2: Arduino_Pro_Micro.D2, OLED.pin1
  N3: Arduino_Pro_Micro.D3, OLED.pin2
  N4: Arduino_Pro_Micro.D9, S1.4
  N5: Arduino_Pro_Micro.D10, Buzzer.1
  N6: Arduino_Pro_Micro.VCC, OLED.pin4
  N7: Arduino_Pro_Micro.RST, S2.2

custom parts:
  Arduino Pro micro: Arduino compatible microcontroller. http://www.modifiedelectronics.com
